# Fritzing sketch skjema (saved by Fritzing 0.9.3b)
breadboards: 1

parts:
  Part1 = Photon
  Part3 = TFT 1.8 inch 160x128 w microSD [part_number=358]

nets:
  N1: Part1.A0, Part3.TFTCS
  N2: Part1.A2, Part3.TFTDC
  N3: Part1.A3, Part3.SCLK
  N4: Part1.A5, Part3.MOSI
  N5: Part1.GND, Part3.LITE
  N6: Part1.D0, Part3.CARDCS

notes:
  ->GND, VCC, SCL, SDA, RES, DC, CS, BLK

custom parts:
  TFT 1.8 inch 160x128 w microSD: This lovely little display breakout is the best way to add a small, colorful and bright display to any project. Since the display uses 4-wire SPI to communicate and has its own pixel-addressable frame buffer, it can be used with every kind of microcontroller. Even a very small one with low memory and few pins available! The 1.8" display has 128x160 color pixels.
